// Logisim project Cond.circ as structural Verilog: 1 circuit, main circuit main
module main (
  input  ZF,
  input  [2:0] ifun,
  input  SF,
  input  OF,
  output out_5
);

  wire and_1_out, decoder_1_out0, decoder_1_out1, decoder_1_out2, decoder_1_out3, decoder_1_out4,
       decoder_1_out5, decoder_1_out6, je_out, jg_out, jge_out, jl_out, jle_out, not_1_out, not_2_out,
       not_3_out, not_4_out, OF____nSF_out, or_1_out, or_2_out, SF____nOF_out;

  not not_1 (not_1_out, SF);
  not not_2 (not_2_out, OF);
  not not_3 (not_3_out, ZF);
  Decoder #(.select(3)) decoder_1 (
    .out0(decoder_1_out0), .out1(decoder_1_out1), .out2(decoder_1_out2), .out3(decoder_1_out3),
    .out4(decoder_1_out4), .out5(decoder_1_out5), .out6(decoder_1_out6), .sel(ifun));  // open: out7, en
  and SF____nOF (SF____nOF_out, SF, SF, not_2_out);
  and OF____nSF (OF____nSF_out, OF, not_1_out);
  not not_4 (not_4_out, or_1_out);
  or or_1 (or_1_out, SF____nOF_out, OF____nSF_out);
  and jg (jg_out, decoder_1_out6, not_3_out, not_4_out);
  and jge (jge_out, decoder_1_out5, not_4_out);
  and je (je_out, ZF, decoder_1_out3);
  and and_1 (and_1_out, not_3_out, decoder_1_out4);
  or or_2 (or_2_out, ZF, or_1_out);
  and jl (jl_out, decoder_1_out2, or_1_out);
  and jle (jle_out, decoder_1_out1, or_2_out);
  or or_3 (out_5, decoder_1_out0, jg_out, jge_out, je_out, and_1_out, jl_out, jle_out);

  // Notes on the sheet:
  //   Cond(CC, ifun)
  //   1
  //   2
  //   3
  //   4
  //   5
  //   6
  //   7
  //   jne
  //   000 = jmp
  //   001 = jle
  //   010 = jl
  //   011 = je
  //   100 = jne
  //   101 = jge
  //   110 = jg
  //   1 = jmp; 0 = don't
endmodule
