// Logisim project Mux4.circ as structural Verilog: 1 circuit, main circuit main
module main (
  input  [31:0] in_1,
  input  [31:0] in_2,
  input  in_3,
  input  [31:0] in_4,
  input  in_5,
  input  [31:0] in_6,
  input  in_7,
  input  in_8,
  input  in_9,
  output [31:0] out_10,
  output out_11
);

  wire [31:0] multiplexer_1_out, multiplexer_2_out;

  Multiplexer #(.width(32), .enable("false")) multiplexer_1 (
    .in0(in_1), .in1(in_2), .out(multiplexer_1_out), .sel(in_5));
  Multiplexer #(.width(32), .enable("false")) multiplexer_2 (
    .in0(in_4), .in1(in_6), .out(multiplexer_2_out), .sel(in_5));
  Multiplexer #(.width(32), .enable("false")) multiplexer_3 (
    .in0(multiplexer_1_out), .in1(multiplexer_2_out), .out(out_10), .sel(in_3));
  Multiplexer #(.enable("false")) multiplexer_4 (.in0(in_7), .in1(in_8), .out(out_11), .sel(in_9));

  // Notes on the sheet:
  //   4-Way 32-bit multiplexer made from three 2-way multiplexers
  //   One-bit, 2-way multiplexer
endmodule
